# Fritzing sketch automatic watering controller (saved by Fritzing 0.9.9b)
circuit board: 28.5185cm x 20.0927cm

parts:
  Arduino = Arduino Uno (Rev3) - ICSP
  DataLogger = Memoire 1.0 - SD card log shield
  Moisture_sensor_1 = Soil Moisture Sensor
  Moisture_Sensor_2 = Soil Moisture Sensor
  Moisture_Sensor_3 = Soil Moisture Sensor
  Moisture_Sensor_4 = Soil Moisture Sensor
  S2_(XB7-NA_5) = SWITCH-MOMENTARY-2 [package=tactile-pth]
  S1_(XB7-NH_5) = Pushbutton [package="[SMD]"]
  Terminal_1 = Camdenboss CTB0158-12 [part_number=CTB0158-12 package=THT]
  R2 = Resistor [tolerance=±5% power=0.25 resistance=10k package=THT]
  R1 = Resistor [tolerance=±5% power=0.25 resistance=10k package=THT]
  5V_relay1 = RELAY [package=relay-t9a]
  Terminal_2 = Camdenboss CTB0158-12 [part_number=CTB0158-12 package=THT]
  5V_relay2 = RELAY [package=relay-t9a]
  V1 = AC Power [voltage=220 frequency=50Hz]
  AC_pump = gear-motor
  Switching_power = DC Power [voltage=12V frequency=60]
  12V_solenoid = Solenoid

nets:
  N1: Arduino.A0, DataLogger.A_IN_0, Terminal_1.pin8
  N2: Arduino.A1, DataLogger.A_IN_1, Terminal_1.pin9
  N3: Arduino.A2, DataLogger.A_IN_2, Terminal_1.pin10
  N4: Arduino.A3, DataLogger.A_IN_3, Terminal_1.pin11
  N5: Arduino.A4/SDA, DataLogger.A_IN_4
  N6: Arduino.A5/SCL, DataLogger.A_IN_5
  GND: Arduino.GND, DataLogger.GND, Terminal_1.pin7
  N7: Arduino.D8, DataLogger.DIG_8
  N8: Arduino.D9_PWM, DataLogger.DIG_9
  N9: Arduino.D10_PWM/SS, DataLogger.DIG_10
  N10: Arduino.D11_PWM/MOSI, DataLogger.DIG_11
  N11: Arduino.D12/MISO, DataLogger.DIG_12
  N12: Arduino.D13/SCK, DataLogger.DIG_13
  N13: Arduino.AREF, DataLogger.AREF
  N14: Arduino.D0/RX, DataLogger.DIG_0
  N15: Arduino.D1/TX, DataLogger.DIG_1
  N16: Arduino.D2, DataLogger.DIG_2, S1_(XB7-NH_5).Pin_1, S1_(XB7-NH_5).Pin_2, Terminal_1.pin1
  N17: Arduino.D3_PWM, DataLogger.DIG_3, S2_(XB7-NA_5).2, Terminal_1.pin2
  N18: Arduino.D4, DataLogger.DIG_4, Terminal_2.pin2
  N19: Arduino.D5_PWM, DataLogger.DIG_5, Terminal_2.pin3
  N20: Arduino.D6_PWM, DataLogger.DIG_6
  N21: Arduino.D7, DataLogger.DIG_7
  N22: Arduino.RESET, DataLogger.RESET
  3V3: Arduino.3V3, DataLogger.3V3
  5V: Arduino.5V, DataLogger.+5V, Terminal_1.pin6, Terminal_2.pin1
  VIN: Arduino.VIN, DataLogger.VIN
  VCC: Moisture_sensor_1.VCC, Moisture_Sensor_2.VCC, Moisture_Sensor_3.VCC, Moisture_Sensor_4.VCC, Terminal_1.terminal_6
  GND_2: Moisture_sensor_1.GND, Moisture_Sensor_2.GND, Moisture_Sensor_3.GND, Moisture_Sensor_4.GND, Terminal_1.terminal_7, R2.Pin_1, R1.Pin_1
  N23: Moisture_sensor_1.SIG, Terminal_1.terminal_8
  N24: Moisture_Sensor_2.SIG, Terminal_1.terminal_9
  N25: Moisture_Sensor_3.SIG, Terminal_1.terminal_10
  N26: Moisture_Sensor_4.SIG, Terminal_1.terminal_11
  N27: S2_(XB7-NA_5).1, S1_(XB7-NH_5).Pin_3, S1_(XB7-NH_5).Pin_4
  N28: Terminal_1.terminal_1, R1.Pin_0
  N29: Terminal_1.terminal_2, R2.Pin_0
  N30: 5V_relay1.COIL1, Terminal_2.terminal_1, 5V_relay2.COIL1
  N31: 5V_relay1.COIL2, Terminal_2.terminal_2
  N32: 5V_relay1.MAIN, Terminal_2.terminal_6
  N33: 5V_relay1.NO, Terminal_2.terminal_5
  N34: Terminal_2.pin5, 12V_solenoid.pin1
  N35: Terminal_2.pin6, Switching_power.V+
  N36: Terminal_2.pin9, V1.V-
  N37: Terminal_2.pin11, AC_pump.pin_1
  N38: Terminal_2.pin12, V1.V+
  N39: Terminal_2.terminal_3, 5V_relay2.COIL2
  N40: Terminal_2.terminal_9, AC_pump.pin_2
  N41: Terminal_2.terminal_11, 5V_relay2.NC
  N42: Terminal_2.terminal_12, 5V_relay2.MAIN
  N43: Switching_power.V-, 12V_solenoid.pin2
